# Fritzing sketch Untitled Sketch (saved by Fritzing 0.9.3b)
breadboards: 1

parts:
  Componente1 = Arduino Uno (Rev3)
  S1 = Pushbutton [package="[SMD]"]
  R1 = Resistor [tolerance=±5% resistance=220 package="2512 [SMD]"]
  LED1 = RGB LED - (4 legs) [package="5 mm [THT]"]
  R2 = Resistor [tolerance=±5% resistance=220 package=THT]
  R3 = Resistor [tolerance=±5% resistance=220 package=THT]
  R4 = Resistor [tolerance=±5% resistance=220 package=THT]
  PIR1 = PIR sensor
  LED2 = smd LED [color="Red (633nm)" package="0805 [SMD]"]
  R5 = Resistor [tolerance=±5% resistance=220 package="2512 [SMD]"]
  KEYPAD1 = Membrane Matrix Keypad

nets:
  N1: Componente1.D8, KEYPAD1.2
  N2: Componente1.D9_PWM, KEYPAD1.1
  N3: Componente1.D10_PWM/SS, R4.Pin_1
  N4: Componente1.D11_PWM/MOSI, S1.Pin_3, S1.Pin_4, R1.Pin_1
  N5: Componente1.D12/MISO, R3.Pin_1
  N6: Componente1.D13/SCK, R2.Pin_1
  N7: Componente1.D1/TX, LED2.anode
  N8: Componente1.D2, PIR1.SIG
  N9: Componente1.D3_PWM, KEYPAD1.7
  N10: Componente1.D4, KEYPAD1.6
  N11: Componente1.D5_PWM, KEYPAD1.5
  N12: Componente1.D6_PWM, KEYPAD1.4
  N13: Componente1.D7, KEYPAD1.3
  5V: Componente1.5V, S1.Pin_1, S1.Pin_2, PIR1.VDD
  GND: Componente1.GND, R1.Pin_0, PIR1.GND, R5.Pin_0
  N14: LED1.red_cathode, R2.Pin_0
  N15: LED1.green_cathode, R3.Pin_0
  N16: LED1.blue_cathode, R4.Pin_0
  N17: LED2.cathode, R5.Pin_1

custom parts:
  Membrane Matrix Keypad: Membrane Matrix 3x4 Keypad
